// Logisim project registrador-paralelo-8-bits.circ as structural Verilog: 1 circuit, main circuit main
module main (
  input  D0,
  input  D1,
  input  D2,
  input  D3,
  input  D4,
  input  D5,
  input  D6,
  input  D7,
  output Q0,
  output Q1,
  output not_Q,
  output Q2,
  output Q3,
  output Q4,
  output Q5,
  output Q6,
  output Q7,
  output not_Q_2,
  output not_Q_3,
  output not_Q_4,
  output not_Q_5,
  output not_Q_6,
  output not_Q_7,
  output not_Q_8
);

  wire and_1_out, and_2_out, and_3_out, and_4_out, and_5_out, and_6_out, and_7_out, and_8_out, and_9_out,
       and_10_out, and_11_out, and_12_out, and_13_out, and_14_out, and_15_out, and_16_out, and_17_out,
       and_18_out, and_19_out, and_20_out, and_21_out, and_22_out, and_23_out, and_24_out, and_25_out,
       and_26_out, and_27_out, and_28_out, and_29_out, and_30_out, and_31_out, and_32_out, and_33_out,
       and_34_out, and_35_out, and_36_out, and_37_out, and_38_out, and_39_out, and_40_out, and_41_out,
       and_42_out, and_43_out, and_44_out, and_45_out, and_46_out, and_47_out, and_48_out, and_49_out,
       and_50_out, and_51_out, and_52_out, and_53_out, and_54_out, and_55_out, and_56_out, and_57_out,
       and_58_out, and_59_out, and_60_out, and_61_out, and_62_out, and_63_out, and_64_out, Clock_out,
       not_1_out, not_2_out, not_3_out, not_4_out, not_5_out, not_6_out, not_7_out, not_8_out, not_9_out,
       not_11_out, not_12_out, not_14_out, not_15_out, not_17_out, not_18_out, not_20_out, not_21_out,
       not_23_out, not_24_out, not_26_out, not_27_out, not_29_out, not_30_out, not_32_out, not_33_out,
       not_34_out, not_35_out, not_36_out, not_37_out, not_38_out, not_39_out, not_40_out, not_41_out,
       not_43_out, not_45_out, not_47_out, not_49_out, not_51_out, not_53_out, not_55_out, or_1_out,
       or_2_out, or_3_out, or_4_out, or_5_out, or_6_out, or_7_out, or_8_out, or_9_out, or_10_out, or_11_out,
       or_12_out, or_13_out, or_14_out, or_15_out, or_16_out, or_17_out, or_18_out, or_19_out, or_20_out,
       or_21_out, or_22_out, or_23_out, or_24_out, or_25_out, or_26_out, or_27_out, or_28_out, or_29_out,
       or_30_out, or_31_out, or_32_out;

  Clock Clock (.out(Clock_out));
  not not_1 (not_1_out, D0);
  not not_2 (not_2_out, D1);
  not not_3 (not_3_out, D2);
  not not_4 (not_4_out, D3);
  not not_5 (not_5_out, D4);
  not not_6 (not_6_out, D5);
  not not_7 (not_7_out, D6);
  not not_8 (not_8_out, D7);
  and and_1 (and_1_out, D0, not_9_out);
  and and_2 (and_2_out, not_9_out, not_1_out);
  and and_3 (and_3_out, D1, not_12_out);
  and and_4 (and_4_out, not_12_out, not_2_out);
  and and_5 (and_5_out, D2, not_15_out);
  and and_6 (and_6_out, not_15_out, not_3_out);
  and and_7 (and_7_out, D3, not_18_out);
  and and_8 (and_8_out, not_18_out, not_4_out);
  and and_9 (and_9_out, D4, not_21_out);
  and and_10 (and_10_out, not_21_out, not_5_out);
  and and_11 (and_11_out, D5, not_24_out);
  and and_12 (and_12_out, not_24_out, not_6_out);
  and and_13 (and_13_out, D6, not_27_out);
  and and_14 (and_14_out, not_27_out, not_7_out);
  and and_15 (and_15_out, D7, not_30_out);
  and and_16 (and_16_out, not_30_out, not_8_out);
  and and_17 (and_17_out, and_1_out, not_9_out);
  and and_18 (and_18_out, not_9_out, and_2_out);
  and and_19 (and_19_out, and_3_out, not_12_out);
  and and_20 (and_20_out, not_12_out, and_4_out);
  and and_21 (and_21_out, and_5_out, not_15_out);
  and and_22 (and_22_out, not_15_out, and_6_out);
  and and_23 (and_23_out, and_7_out, not_18_out);
  and and_24 (and_24_out, not_18_out, and_8_out);
  and and_25 (and_25_out, and_9_out, not_21_out);
  and and_26 (and_26_out, not_21_out, and_10_out);
  and and_27 (and_27_out, and_11_out, not_24_out);
  and and_28 (and_28_out, not_24_out, and_12_out);
  and and_29 (and_29_out, and_13_out, not_27_out);
  and and_30 (and_30_out, not_27_out, and_14_out);
  and and_31 (and_31_out, and_15_out, not_30_out);
  and and_32 (and_32_out, not_30_out, and_16_out);
  not not_9 (not_9_out, Clock_out);
  or or_1 (or_1_out, and_17_out, not_11_out);
  not not_10 (not_Q, or_1_out);
  or or_2 (or_2_out, not_Q, and_18_out);
  not not_11 (not_11_out, or_2_out);
  not not_12 (not_12_out, Clock_out);
  or or_3 (or_3_out, and_19_out, not_14_out);
  not not_13 (not_Q_2, or_3_out);
  or or_4 (or_4_out, not_Q_2, and_20_out);
  not not_14 (not_14_out, or_4_out);
  not not_15 (not_15_out, Clock_out);
  or or_5 (or_5_out, and_21_out, not_17_out);
  not not_16 (not_Q_3, or_5_out);
  not not_17 (not_17_out, or_6_out);
  or or_6 (or_6_out, not_Q_3, and_22_out);
  not not_18 (not_18_out, Clock_out);
  or or_7 (or_7_out, and_23_out, not_20_out);
  not not_19 (not_Q_4, or_7_out);
  not not_20 (not_20_out, or_8_out);
  or or_8 (or_8_out, not_Q_4, and_24_out);
  not not_21 (not_21_out, Clock_out);
  or or_9 (or_9_out, and_25_out, not_23_out);
  not not_22 (not_Q_5, or_9_out);
  not not_23 (not_23_out, or_10_out);
  or or_10 (or_10_out, not_Q_5, and_26_out);
  not not_24 (not_24_out, Clock_out);
  or or_11 (or_11_out, and_27_out, not_26_out);
  not not_25 (not_Q_6, or_11_out);
  or or_12 (or_12_out, not_Q_6, and_28_out);
  not not_26 (not_26_out, or_12_out);
  not not_27 (not_27_out, Clock_out);
  or or_13 (or_13_out, and_29_out, not_29_out);
  not not_28 (not_Q_7, or_13_out);
  not not_29 (not_29_out, or_14_out);
  or or_14 (or_14_out, not_Q_7, and_30_out);
  not not_30 (not_30_out, Clock_out);
  or or_15 (or_15_out, and_31_out, not_32_out);
  not not_31 (not_Q_8, or_15_out);
  or or_16 (or_16_out, not_Q_8, and_32_out);
  not not_32 (not_32_out, or_16_out);
  not not_33 (not_33_out, not_11_out);
  not not_34 (not_34_out, not_14_out);
  not not_35 (not_35_out, not_17_out);
  not not_36 (not_36_out, not_20_out);
  not not_37 (not_37_out, not_23_out);
  not not_38 (not_38_out, not_26_out);
  not not_39 (not_39_out, not_29_out);
  not not_40 (not_40_out, not_32_out);
  and and_33 (and_33_out, not_11_out, Clock_out);
  and and_34 (and_34_out, Clock_out, not_33_out);
  and and_35 (and_35_out, not_14_out, Clock_out);
  and and_36 (and_36_out, Clock_out, not_34_out);
  and and_37 (and_37_out, not_17_out, Clock_out);
  and and_38 (and_38_out, Clock_out, not_35_out);
  and and_39 (and_39_out, not_20_out, Clock_out);
  and and_40 (and_40_out, Clock_out, not_36_out);
  and and_41 (and_41_out, not_23_out, Clock_out);
  and and_42 (and_42_out, Clock_out, not_37_out);
  and and_43 (and_43_out, not_26_out, Clock_out);
  and and_44 (and_44_out, Clock_out, not_38_out);
  and and_45 (and_45_out, not_29_out, Clock_out);
  and and_46 (and_46_out, Clock_out, not_39_out);
  and and_47 (and_47_out, not_32_out, Clock_out);
  and and_48 (and_48_out, Clock_out, not_40_out);
  and and_49 (and_49_out, and_33_out, Clock_out);
  and and_50 (and_50_out, Clock_out, and_34_out);
  and and_51 (and_51_out, and_35_out, Clock_out);
  and and_52 (and_52_out, Clock_out, and_36_out);
  and and_53 (and_53_out, and_37_out, Clock_out);
  and and_54 (and_54_out, Clock_out, and_38_out);
  and and_55 (and_55_out, and_39_out, Clock_out);
  and and_56 (and_56_out, Clock_out, and_40_out);
  and and_57 (and_57_out, and_41_out, Clock_out);
  and and_58 (and_58_out, Clock_out, and_42_out);
  and and_59 (and_59_out, and_43_out, Clock_out);
  and and_60 (and_60_out, Clock_out, and_44_out);
  and and_61 (and_61_out, and_45_out, Clock_out);
  and and_62 (and_62_out, Clock_out, and_46_out);
  and and_63 (and_63_out, and_47_out, Clock_out);
  and and_64 (and_64_out, Clock_out, and_48_out);
  or or_17 (or_17_out, and_49_out, Q0);
  not not_41 (not_41_out, or_17_out);
  or or_18 (or_18_out, not_41_out, and_50_out);
  not not_42 (Q0, or_18_out);
  or or_19 (or_19_out, and_51_out, Q1);
  not not_43 (not_43_out, or_19_out);
  or or_20 (or_20_out, not_43_out, and_52_out);
  not not_44 (Q1, or_20_out);
  or or_21 (or_21_out, and_53_out, Q2);
  not not_45 (not_45_out, or_21_out);
  not not_46 (Q2, or_22_out);
  or or_22 (or_22_out, not_45_out, and_54_out);
  or or_23 (or_23_out, and_55_out, Q3);
  not not_47 (not_47_out, or_23_out);
  or or_24 (or_24_out, not_47_out, and_56_out);
  not not_48 (Q3, or_24_out);
  or or_25 (or_25_out, and_57_out, Q4);
  not not_49 (not_49_out, or_25_out);
  or or_26 (or_26_out, not_49_out, and_58_out);
  not not_50 (Q4, or_26_out);
  or or_27 (or_27_out, and_59_out, Q5);
  not not_51 (not_51_out, or_27_out);
  not not_52 (Q5, or_28_out);
  or or_28 (or_28_out, not_51_out, and_60_out);
  or or_29 (or_29_out, and_61_out, Q6);
  not not_53 (not_53_out, or_29_out);
  not not_54 (Q6, or_30_out);
  or or_30 (or_30_out, not_53_out, and_62_out);
  or or_31 (or_31_out, and_63_out, Q7);
  not not_55 (not_55_out, or_31_out);
  not not_56 (Q7, or_32_out);
  or or_32 (or_32_out, not_55_out, and_64_out);

  // Notes on the sheet:
  //   S
  //   R
  //   S
  //   R
  //   S
  //   R
  //   S
  //   R
  //   S
  //   R
  //   S
  //   R
  //   S
  //   R
  //   S
  //   R
  //   Q
  //   Q
  //   Q
  //   Q
  //   Q
  //   Q
  //   Q
  //   Q
  //   S
  //   R
  //   S
  //   R
  //   S
  //   R
  //   S
  //   R
  //   S
  //   R
  //   S
  //   R
  //   S
  //   R
  //   S
  //   R
endmodule
