// Logisim project resumo-semestre.circ as structural Verilog: 10 circuits, main circuit main
module main (
  input  A,
  input  B,
  input  Clock,
  input  S,
  input  D0,
  input  Clock_2,
  input  R,
  input  D1,
  input  D,
  input  Clock_3,
  input  D2,
  input  Clock_4,
  input  D_2,
  input  D3,
  input  Clock_5,
  input  D0_2,
  input  D0_3,
  input  D1_2,
  input  D5,
  input  D2_2,
  input  D6,
  input  D3_2,
  input  D7,
  output AND,
  output out_25,
  output out_26,
  output XOR,
  output out_28,
  output out_29,
  output out_30,
  output out_31,
  output out_32,
  output out_33,
  output not_Q,
  output not_Q_2,
  output Q,
  output Q0,
  output not_Q_3,
  output not_Q_4,
  output Q1,
  output Q_2,
  output not_Q_5,
  output not_Q_6,
  output Q2,
  output Q0_2,
  output not_Q_7,
  output Q3,
  output not_Q_8,
  output not_Q_9,
  output Q0_3,
  output Q4,
  output not_Q_10,
  output not_Q_11,
  output Q1_2,
  output Q5,
  output not_Q_12,
  output not_Q_13,
  output Q2_2,
  output Q6,
  output not_Q_14,
  output not_Q_15,
  output Q3_2,
  output Q7
);

  wire and_1_out, and_2_out, and_3_out, and_4_out, and_5_out, and_6_out, and_7_out, and_8_out, and_9_out,
       and_10_out, and_12_out, and_13_out, and_14_out, and_15_out, and_16_out, and_17_out, and_18_out,
       and_19_out, and_20_out, and_21_out, and_22_out, and_23_out, and_24_out, and_25_out, and_26_out,
       and_27_out, and_28_out, and_29_out, and_30_out, and_31_out, and_32_out, and_33_out, and_34_out,
       and_35_out, and_36_out, and_37_out, and_38_out, and_39_out, and_40_out, and_41_out, and_42_out,
       and_43_out, and_44_out, and_45_out, and_46_out, and_47_out, and_48_out, and_49_out, and_50_out,
       and_51_out, and_52_out, and_53_out, and_54_out, and_55_out, and_56_out, and_57_out, and_58_out,
       and_59_out, and_60_out, and_61_out, and_62_out, and_63_out, and_64_out, and_65_out, and_66_out,
       and_67_out, and_68_out, and_69_out, and_70_out, and_71_out, and_72_out, and_73_out, and_74_out,
       and_75_out, and_76_out, and_77_out, and_78_out, and_79_out, and_80_out, and_81_out, and_82_out,
       and_83_out, and_84_out, and_85_out, and_86_out, and_87_out, and_88_out, and_89_out, and_90_out,
       and_91_out, and_92_out, and_93_out, and_94_out, and_95_out, and_96_out, and_97_out, and_98_out,
       and_99_out, and_100_out, and_101_out, and_102_out, and_103_out, and_104_out, and_105_out, and_106_out,
       and_107_out, and_108_out, and_109_out, and_110_out, and_111_out, and_112_out, and_113_out,
       and_114_out, not_1_out, not_2_out, not_3_out, not_4_out, not_5_out, not_6_out, not_7_out, not_8_out,
       not_9_out, not_10_out, not_11_out, not_12_out, not_13_out, not_17_out, not_19_out, not_21_out,
       not_23_out, not_25_out, not_26_out, not_27_out, not_28_out, not_29_out, not_30_out, not_36_out,
       not_38_out, not_40_out, not_42_out, not_44_out, not_46_out, not_47_out, not_48_out, not_49_out,
       not_50_out, not_51_out, not_52_out, not_53_out, not_54_out, not_55_out, not_56_out, not_57_out,
       not_58_out, not_59_out, not_60_out, not_61_out, not_63_out, not_65_out, not_67_out, not_69_out,
       not_71_out, not_73_out, not_75_out, not_77_out, not_78_out, not_79_out, not_80_out, not_81_out,
       not_82_out, not_83_out, not_84_out, not_85_out, not_86_out, not_88_out, not_90_out, not_92_out,
       not_94_out, not_96_out, not_98_out, not_100_out, or_2_out, or_3_out, or_4_out, or_5_out, or_6_out,
       or_7_out, or_8_out, or_9_out, or_10_out, or_11_out, or_12_out, or_13_out, or_14_out, or_16_out,
       or_17_out, or_18_out, or_19_out, or_20_out, or_21_out, or_22_out, or_23_out, or_24_out, or_25_out,
       or_26_out, or_27_out, or_28_out, or_29_out, or_30_out, or_31_out, or_32_out, or_33_out, or_34_out,
       or_35_out, or_36_out, or_37_out, or_38_out, or_39_out, or_40_out, or_41_out, or_42_out, or_43_out,
       or_44_out, or_45_out, or_46_out, or_47_out, or_48_out, or_49_out, or_50_out, or_51_out, or_52_out,
       or_53_out, or_54_out, or_55_out, or_56_out, or_57_out, or_58_out, or_59_out, xor_2_out;

  not not_1 (not_1_out, D_2);
  not not_2 (not_2_out, D0_2);
  not not_3 (not_3_out, D1_2);
  not not_4 (not_4_out, D2_2);
  not not_5 (not_5_out, D3_2);
  not not_6 (not_6_out, D);
  and and_1 (and_1_out, D_2, not_7_out);
  and and_2 (and_2_out, not_7_out, not_1_out);
  and and_3 (and_3_out, D0_2, not_8_out);
  and and_4 (and_4_out, not_8_out, not_2_out);
  and and_5 (and_5_out, D1_2, not_9_out);
  and and_6 (and_6_out, not_9_out, not_3_out);
  and and_7 (and_7_out, D2_2, not_10_out);
  and and_8 (and_8_out, not_10_out, not_4_out);
  and and_9 (and_9_out, D3_2, not_11_out);
  and and_10 (and_10_out, not_11_out, not_5_out);
  and and_11 (AND, A, B);
  or or_1 (out_25, A, B);
  xor xor_1 (XOR, A, B);
  nand NAND (out_28, A, B);
  xnor XNOR (out_30, A, B);
  nor NOR (out_32, A, B);
  and and_12 (and_12_out, S, Clock_2);
  and and_13 (and_13_out, Clock_2, R);
  and and_14 (and_14_out, D, Clock_3);
  and and_15 (and_15_out, Clock_3, not_6_out);
  and and_16 (and_16_out, and_1_out, not_7_out);
  and and_17 (and_17_out, not_7_out, and_2_out);
  and and_18 (and_18_out, and_3_out, not_8_out);
  and and_19 (and_19_out, not_8_out, and_4_out);
  and and_20 (and_20_out, and_5_out, not_9_out);
  and and_21 (and_21_out, not_9_out, and_6_out);
  and and_22 (and_22_out, and_7_out, not_10_out);
  and and_23 (and_23_out, not_10_out, and_8_out);
  and and_24 (and_24_out, and_9_out, not_11_out);
  and and_25 (and_25_out, not_11_out, and_10_out);
  or or_2 (or_2_out, and_12_out, Q);
  or or_3 (or_3_out, not_Q, and_13_out);
  not not_7 (not_7_out, Clock_4);
  or or_4 (or_4_out, and_16_out, not_17_out);
  or or_5 (or_5_out, not_Q_6, and_17_out);
  not not_8 (not_8_out, Clock_5);
  or or_6 (or_6_out, and_18_out, not_19_out);
  or or_7 (or_7_out, not_Q_8, and_19_out);
  not not_9 (not_9_out, Clock_5);
  or or_8 (or_8_out, and_20_out, not_21_out);
  or or_9 (or_9_out, not_Q_10, and_21_out);
  not not_10 (not_10_out, Clock_5);
  or or_10 (or_10_out, and_22_out, not_23_out);
  or or_11 (or_11_out, not_Q_12, and_23_out);
  not not_11 (not_11_out, Clock_5);
  or or_12 (or_12_out, and_24_out, not_25_out);
  or or_13 (or_13_out, not_Q_14, and_25_out);
  not not_12 (not_12_out, A);
  not not_13 (not_13_out, B);
  not not_14 (not_Q, or_2_out);
  not not_15 (Q, or_3_out);
  not not_16 (not_Q_6, or_4_out);
  not not_17 (not_17_out, or_5_out);
  not not_18 (not_Q_8, or_6_out);
  not not_19 (not_19_out, or_7_out);
  not not_20 (not_Q_10, or_8_out);
  not not_21 (not_21_out, or_9_out);
  not not_22 (not_Q_12, or_10_out);
  not not_23 (not_23_out, or_11_out);
  not not_24 (not_Q_14, or_12_out);
  not not_25 (not_25_out, or_13_out);
  and and_26 (and_26_out, not_12_out, B);
  and and_27 (and_27_out, A, not_13_out);
  and and_28 (and_28_out, A, B);
  xor xor_2 (xor_2_out, A, B);
  or or_14 (or_14_out, A, B);
  and and_29 (and_29_out, and_14_out, Clock_3);
  and and_30 (and_30_out, Clock_3, and_15_out);
  not not_26 (not_26_out, not_17_out);
  not not_27 (not_27_out, not_19_out);
  not not_28 (not_28_out, not_21_out);
  not not_29 (not_29_out, not_23_out);
  not not_30 (not_30_out, not_25_out);
  or or_15 (out_26, and_26_out, and_27_out);
  not not_31 (out_29, and_28_out);
  not not_32 (out_31, xor_2_out);
  not not_33 (out_33, or_14_out);
  and and_31 (and_31_out, not_17_out, Clock_4);
  and and_32 (and_32_out, Clock_4, not_26_out);
  and and_33 (and_33_out, not_19_out, Clock_5);
  and and_34 (and_34_out, Clock_5, not_27_out);
  and and_35 (and_35_out, not_21_out, Clock_5);
  and and_36 (and_36_out, Clock_5, not_28_out);
  and and_37 (and_37_out, not_23_out, Clock_5);
  and and_38 (and_38_out, Clock_5, not_29_out);
  and and_39 (and_39_out, not_25_out, Clock_5);
  and and_40 (and_40_out, Clock_5, not_30_out);
  or or_16 (or_16_out, and_29_out, Q_2);
  not not_34 (not_Q_4, or_16_out);
  or or_17 (or_17_out, not_Q_4, and_30_out);
  not not_35 (Q_2, or_17_out);
  and and_41 (and_41_out, and_31_out, Clock_4);
  and and_42 (and_42_out, Clock_4, and_32_out);
  and and_43 (and_43_out, and_33_out, Clock_5);
  and and_44 (and_44_out, Clock_5, and_34_out);
  and and_45 (and_45_out, and_35_out, Clock_5);
  and and_46 (and_46_out, Clock_5, and_36_out);
  and and_47 (and_47_out, and_37_out, Clock_5);
  and and_48 (and_48_out, Clock_5, and_38_out);
  and and_49 (and_49_out, and_39_out, Clock_5);
  and and_50 (and_50_out, Clock_5, and_40_out);
  or or_18 (or_18_out, and_41_out, Q0_2);
  or or_19 (or_19_out, not_36_out, and_42_out);
  or or_20 (or_20_out, and_43_out, Q0_3);
  or or_21 (or_21_out, not_38_out, and_44_out);
  or or_22 (or_22_out, and_45_out, Q1_2);
  or or_23 (or_23_out, not_40_out, and_46_out);
  or or_24 (or_24_out, and_47_out, Q2_2);
  or or_25 (or_25_out, not_42_out, and_48_out);
  or or_26 (or_26_out, and_49_out, Q3_2);
  or or_27 (or_27_out, not_44_out, and_50_out);
  not not_36 (not_36_out, or_18_out);
  not not_37 (Q0_2, or_19_out);
  not not_38 (not_38_out, or_20_out);
  not not_39 (Q0_3, or_21_out);
  not not_40 (not_40_out, or_22_out);
  not not_41 (Q1_2, or_23_out);
  not not_42 (not_42_out, or_24_out);
  not not_43 (Q2_2, or_25_out);
  not not_44 (not_44_out, or_26_out);
  not not_45 (Q3_2, or_27_out);
  and and_51 (and_51_out, D0, not_54_out);
  and and_52 (and_52_out, not_54_out, not_46_out);
  not not_46 (not_46_out, D0);
  and and_53 (and_53_out, D1, not_55_out);
  and and_54 (and_54_out, not_55_out, not_47_out);
  not not_47 (not_47_out, D1);
  and and_55 (and_55_out, D2, not_56_out);
  and and_56 (and_56_out, not_56_out, not_48_out);
  not not_48 (not_48_out, D2);
  and and_57 (and_57_out, D3, not_57_out);
  and and_58 (and_58_out, not_57_out, not_49_out);
  not not_49 (not_49_out, D3);
  and and_59 (and_59_out, D0_3, not_58_out);
  and and_60 (and_60_out, not_58_out, not_50_out);
  not not_50 (not_50_out, D0_3);
  and and_61 (and_61_out, D5, not_59_out);
  and and_62 (and_62_out, not_59_out, not_51_out);
  not not_51 (not_51_out, D5);
  and and_63 (and_63_out, D6, not_60_out);
  and and_64 (and_64_out, not_60_out, not_52_out);
  not not_52 (not_52_out, D6);
  and and_65 (and_65_out, D7, not_61_out);
  and and_66 (and_66_out, not_61_out, not_53_out);
  not not_53 (not_53_out, D7);
  and and_67 (and_67_out, and_51_out, not_54_out);
  and and_68 (and_68_out, not_54_out, and_52_out);
  and and_69 (and_69_out, and_53_out, not_55_out);
  and and_70 (and_70_out, not_55_out, and_54_out);
  and and_71 (and_71_out, and_55_out, not_56_out);
  and and_72 (and_72_out, not_56_out, and_56_out);
  and and_73 (and_73_out, and_57_out, not_57_out);
  and and_74 (and_74_out, not_57_out, and_58_out);
  and and_75 (and_75_out, and_59_out, not_58_out);
  and and_76 (and_76_out, not_58_out, and_60_out);
  and and_77 (and_77_out, and_61_out, not_59_out);
  and and_78 (and_78_out, not_59_out, and_62_out);
  and and_79 (and_79_out, and_63_out, not_60_out);
  and and_80 (and_80_out, not_60_out, and_64_out);
  and and_81 (and_81_out, and_65_out, not_61_out);
  and and_82 (and_82_out, not_61_out, and_66_out);
  not not_54 (not_54_out, Clock);
  or or_28 (or_28_out, and_67_out, not_63_out);
  or or_29 (or_29_out, not_Q_2, and_68_out);
  not not_55 (not_55_out, Clock);
  or or_30 (or_30_out, and_69_out, not_65_out);
  or or_31 (or_31_out, not_Q_3, and_70_out);
  not not_56 (not_56_out, Clock);
  or or_32 (or_32_out, and_71_out, not_67_out);
  or or_33 (or_33_out, not_Q_5, and_72_out);
  not not_57 (not_57_out, Clock);
  or or_34 (or_34_out, and_73_out, not_69_out);
  or or_35 (or_35_out, not_Q_7, and_74_out);
  not not_58 (not_58_out, Clock);
  or or_36 (or_36_out, and_75_out, not_71_out);
  or or_37 (or_37_out, not_Q_9, and_76_out);
  not not_59 (not_59_out, Clock);
  or or_38 (or_38_out, and_77_out, not_73_out);
  or or_39 (or_39_out, not_Q_11, and_78_out);
  not not_60 (not_60_out, Clock);
  or or_40 (or_40_out, and_79_out, not_75_out);
  or or_41 (or_41_out, not_Q_13, and_80_out);
  not not_61 (not_61_out, Clock);
  or or_42 (or_42_out, and_81_out, not_77_out);
  or or_43 (or_43_out, not_Q_15, and_82_out);
  not not_62 (not_Q_2, or_28_out);
  not not_63 (not_63_out, or_29_out);
  not not_64 (not_Q_3, or_30_out);
  not not_65 (not_65_out, or_31_out);
  not not_66 (not_Q_5, or_32_out);
  not not_67 (not_67_out, or_33_out);
  not not_68 (not_Q_7, or_34_out);
  not not_69 (not_69_out, or_35_out);
  not not_70 (not_Q_9, or_36_out);
  not not_71 (not_71_out, or_37_out);
  not not_72 (not_Q_11, or_38_out);
  not not_73 (not_73_out, or_39_out);
  not not_74 (not_Q_13, or_40_out);
  not not_75 (not_75_out, or_41_out);
  not not_76 (not_Q_15, or_42_out);
  not not_77 (not_77_out, or_43_out);
  not not_78 (not_78_out, not_63_out);
  not not_79 (not_79_out, not_65_out);
  not not_80 (not_80_out, not_67_out);
  not not_81 (not_81_out, not_69_out);
  not not_82 (not_82_out, not_71_out);
  not not_83 (not_83_out, not_73_out);
  not not_84 (not_84_out, not_75_out);
  not not_85 (not_85_out, not_77_out);
  and and_83 (and_83_out, not_63_out, Clock);
  and and_84 (and_84_out, Clock, not_78_out);
  and and_85 (and_85_out, not_65_out, Clock);
  and and_86 (and_86_out, Clock, not_79_out);
  and and_87 (and_87_out, not_67_out, Clock);
  and and_88 (and_88_out, Clock, not_80_out);
  and and_89 (and_89_out, not_69_out, Clock);
  and and_90 (and_90_out, Clock, not_81_out);
  and and_91 (and_91_out, not_71_out, Clock);
  and and_92 (and_92_out, Clock, not_82_out);
  and and_93 (and_93_out, not_73_out, Clock);
  and and_94 (and_94_out, Clock, not_83_out);
  and and_95 (and_95_out, not_75_out, Clock);
  and and_96 (and_96_out, Clock, not_84_out);
  and and_97 (and_97_out, not_77_out, Clock);
  and and_98 (and_98_out, Clock, not_85_out);
  and and_99 (and_99_out, and_83_out, Clock);
  and and_100 (and_100_out, Clock, and_84_out);
  and and_101 (and_101_out, and_85_out, Clock);
  and and_102 (and_102_out, Clock, and_86_out);
  and and_103 (and_103_out, and_87_out, Clock);
  and and_104 (and_104_out, Clock, and_88_out);
  and and_105 (and_105_out, and_89_out, Clock);
  and and_106 (and_106_out, Clock, and_90_out);
  and and_107 (and_107_out, and_91_out, Clock);
  and and_108 (and_108_out, Clock, and_92_out);
  and and_109 (and_109_out, and_93_out, Clock);
  and and_110 (and_110_out, Clock, and_94_out);
  and and_111 (and_111_out, and_95_out, Clock);
  and and_112 (and_112_out, Clock, and_96_out);
  and and_113 (and_113_out, and_97_out, Clock);
  and and_114 (and_114_out, Clock, and_98_out);
  or or_44 (or_44_out, and_99_out, Q0);
  or or_45 (or_45_out, not_86_out, and_100_out);
  or or_46 (or_46_out, and_101_out, Q1);
  or or_47 (or_47_out, not_88_out, and_102_out);
  or or_48 (or_48_out, and_103_out, Q2);
  or or_49 (or_49_out, not_90_out, and_104_out);
  or or_50 (or_50_out, and_105_out, Q3);
  or or_51 (or_51_out, not_92_out, and_106_out);
  or or_52 (or_52_out, and_107_out, Q4);
  or or_53 (or_53_out, not_94_out, and_108_out);
  or or_54 (or_54_out, and_109_out, Q5);
  or or_55 (or_55_out, not_96_out, and_110_out);
  or or_56 (or_56_out, and_111_out, Q6);
  or or_57 (or_57_out, not_98_out, and_112_out);
  or or_58 (or_58_out, and_113_out, Q7);
  or or_59 (or_59_out, not_100_out, and_114_out);
  not not_86 (not_86_out, or_44_out);
  not not_87 (Q0, or_45_out);
  not not_88 (not_88_out, or_46_out);
  not not_89 (Q1, or_47_out);
  not not_90 (not_90_out, or_48_out);
  not not_91 (Q2, or_49_out);
  not not_92 (not_92_out, or_50_out);
  not not_93 (Q3, or_51_out);
  not not_94 (not_94_out, or_52_out);
  not not_95 (Q4, or_53_out);
  not not_96 (not_96_out, or_54_out);
  not not_97 (Q5, or_55_out);
  not not_98 (not_98_out, or_56_out);
  not not_99 (Q6, or_57_out);
  not not_100 (not_100_out, or_58_out);
  not not_101 (Q7, or_59_out);

  // Notes on the sheet:
  //   OR
  //   S
  //   R
  //   S
  //   R
  //   S
  //   R
  //   S
  //   R
  //   S
  //   R
  //   LOGIC GATES
  //   LATCH SR CLOCK
  //   S
  //   R
  //   FLIP FLOP (1 bit)
  //   LATCH D 1
  //   EQUIVALENT TO >
  //   LATCH D
  //   REGISTRADOR (4 bits)
  //   Q
  //   Q
  //   Q
  //   Q
  //   Q
  //   S
  //   R
  //   S
  //   R
  //   S
  //   R
  //   S
  //   R
  //   S
  //   R
  //   LATCH D 2
  //   S
  //   R
  //   S
  //   R
  //   S
  //   R
  //   S
  //   R
  //   S
  //   R
  //   S
  //   R
  //   S
  //   R
  //   S
  //   R
  //   REGISTRADOR (8 bits)
  //   Q
  //   Q
  //   Q
  //   Q
  //   Q
  //   Q
  //   Q
  //   Q
  //   S
  //   R
  //   S
  //   R
  //   S
  //   R
  //   S
  //   R
  //   S
  //   R
  //   S
  //   R
  //   S
  //   R
  //   S
  //   R
endmodule

module XOR (
  input  A,
  input  B,
  output Y
);

  wire and_1_out, and_2_out, not_1_out, not_2_out;

  not not_1 (not_1_out, A);
  not not_2 (not_2_out, B);
  buf and_1 (and_1_out, not_1_out);  // AND_Gate
  buf and_2 (and_2_out, not_2_out);  // AND_Gate
  or or_1 (Y, and_1_out, and_2_out);
endmodule

module LatchSR (
  input  R,
  input  S,
  output Q_prime,
  output Q
);

  wire or_1_out, or_2_out;

  or or_1 (or_1_out, R, Q);
  or or_2 (or_2_out, Q_prime, S);
  not not_1 (Q_prime, or_1_out);
  not not_2 (Q, or_2_out);
endmodule

module LatchSRClock (
  input  S,
  input  Clock,
  input  R,
  output Q
);

  wire and_1_out, and_2_out;

  and and_1 (and_1_out, S, Clock);
  and and_2 (and_2_out, Clock, R);
  LatchSR latchsr_1 (.R(and_1_out), .S(and_2_out), .Q(Q));  // open: Q_prime

  // Notes on the sheet:
  //   LATCH SR CLOCK
  //   LATCH SR
endmodule

module LatchD (
  input  Clock,
  input  D,
  output Q
);

  wire and_1_out, and_2_out, not_1_out;

  not not_1 (not_1_out, D);
  and and_1 (and_1_out, D, Clock);
  and and_2 (and_2_out, Clock, not_1_out);
  LatchSRClock latchsrclock_1 (.S(and_1_out), .Clock(Clock), .R(and_2_out), .Q(Q));

  // Notes on the sheet:
  //   S
  //   R
  //   LATCH D
endmodule

module _1bitFlipFlop (
  input  Clock,
  input  D,
  output Q
);

  wire latchd_1_q, not_1_out;

  not not_1 (not_1_out, Clock);
  LatchD latchd_1 (.D(D), .Clock(not_1_out), .Q(latchd_1_q));
  LatchD latchd_2 (.D(latchd_1_q), .Clock(Clock), .Q(Q));
endmodule

module _8bitRegister (
  input  Clock,
  input  D0,
  input  D1,
  input  D2,
  input  D3,
  input  D4,
  input  D5,
  input  D6,
  input  D7,
  output Q0,
  output Q1,
  output Q2,
  output Q3,
  output Q4,
  output Q5,
  output Q6,
  output Q7
);

  _1bitFlipFlop u_1bitflipflop_1 (.D(D0), .Q(Q0), .Clock(Clock));
  _1bitFlipFlop u_1bitflipflop_2 (.D(D1), .Q(Q1), .Clock(Clock));
  _1bitFlipFlop u_1bitflipflop_3 (.D(D2), .Q(Q2), .Clock(Clock));
  _1bitFlipFlop u_1bitflipflop_4 (.D(D3), .Q(Q3), .Clock(Clock));
  _1bitFlipFlop u_1bitflipflop_5 (.D(D4), .Q(Q4), .Clock(Clock));
  _1bitFlipFlop u_1bitflipflop_6 (.D(D5), .Q(Q5), .Clock(Clock));
  _1bitFlipFlop u_1bitflipflop_7 (.D(D6), .Q(Q6), .Clock(Clock));
  _1bitFlipFlop u_1bitflipflop_8 (.D(D7), .Q(Q7), .Clock(Clock));
endmodule

module SomadorSubtrator8bits (
  input  M,
  input  A7,
  input  A6,
  input  A5,
  input  A4,
  input  A3,
  input  A2,
  input  A1,
  input  A0,
  input  B7,
  input  B6,
  input  B5,
  input  B4,
  input  B3,
  input  B2,
  input  B1,
  input  B0,
  output Cout,
  output S7,
  output S6,
  output S5,
  output S4,
  output S3,
  output S2,
  output S1,
  output S0
);

  wire fulladder_1_cout, fulladder_2_cout, fulladder_3_cout, fulladder_4_cout, fulladder_5_cout,
       fulladder_6_cout, fulladder_7_cout, xor_1_y, xor_2_y, xor_3_y, xor_4_y, xor_5_y, xor_6_y, xor_7_y,
       xor_8_y;

  XOR xor_1 (.A(B0), .B(M), .Y(xor_1_y));
  XOR xor_2 (.A(B1), .B(M), .Y(xor_2_y));
  XOR xor_3 (.A(B2), .B(M), .Y(xor_3_y));
  XOR xor_4 (.A(B3), .B(M), .Y(xor_4_y));
  XOR xor_5 (.A(B4), .B(M), .Y(xor_5_y));
  XOR xor_6 (.A(B5), .B(M), .Y(xor_6_y));
  XOR xor_7 (.A(B6), .B(M), .Y(xor_7_y));
  XOR xor_8 (.A(B7), .B(M), .Y(xor_8_y));
  FullAdder fulladder_1 (.A(M), .B(A0), .Cin(xor_1_y), .S(S0), .Cout(fulladder_1_cout));
  FullAdder fulladder_2 (.A(fulladder_1_cout), .B(A1), .Cin(xor_2_y), .S(S1), .Cout(fulladder_2_cout));
  FullAdder fulladder_3 (.A(fulladder_2_cout), .B(A2), .Cin(xor_3_y), .S(S2), .Cout(fulladder_3_cout));
  FullAdder fulladder_4 (.A(fulladder_3_cout), .B(A3), .Cin(xor_4_y), .S(S3), .Cout(fulladder_4_cout));
  FullAdder fulladder_5 (.A(fulladder_4_cout), .B(A4), .Cin(xor_5_y), .S(S4), .Cout(fulladder_5_cout));
  FullAdder fulladder_6 (.A(fulladder_5_cout), .B(A5), .Cin(xor_6_y), .S(S5), .Cout(fulladder_6_cout));
  FullAdder fulladder_7 (.A(fulladder_6_cout), .B(A6), .Cin(xor_7_y), .S(S6), .Cout(fulladder_7_cout));
  FullAdder fulladder_8 (.A(fulladder_7_cout), .B(A7), .Cin(xor_8_y), .S(S7), .Cout(Cout));
endmodule

module HalfAdder (
  input  A,
  input  B,
  output Sum,
  output Cout
);

  XOR xor_1 (.A(A), .B(B), .Y(Sum));
  and and_1 (Cout, B, A);
endmodule

module FullAdder (
  input  A,
  input  B,
  input  Cin,
  output S,
  output Cout
);

  wire halfadder_1_cout, halfadder_1_sum, halfadder_2_cout;

  HalfAdder halfadder_1 (.A(A), .B(B), .Sum(halfadder_1_sum), .Cout(halfadder_1_cout));
  HalfAdder halfadder_2 (.A(halfadder_1_sum), .B(Cin), .Sum(S), .Cout(halfadder_2_cout));
  or or_1 (Cout, halfadder_2_cout, halfadder_1_cout);
endmodule
