// Logisim project somador-completo-8-bits-2.circ as structural Verilog: 1 circuit, main circuit main
module main (
  input  Cin,
  input  A0,
  input  A7,
  input  A6,
  input  A5,
  input  A4,
  input  A3,
  input  A2,
  input  A1,
  input  B7,
  input  B6,
  input  B5,
  input  B4,
  input  B3,
  input  B2,
  input  B1,
  input  B0,
  output Cout,
  output S7,
  output S6,
  output S5,
  output S4,
  output S3,
  output S2,
  output S1,
  output S0
);

  wire and_1_out, and_2_out, and_3_out, and_4_out, and_5_out, and_6_out, and_7_out, and_8_out, and_9_out,
       and_10_out, and_11_out, and_12_out, and_13_out, and_14_out, and_15_out, and_16_out, and_17_out,
       and_18_out, and_19_out, and_20_out, and_21_out, and_22_out, and_23_out, and_24_out, and_25_out,
       and_26_out, and_27_out, and_28_out, and_29_out, and_30_out, and_31_out, and_32_out, and_33_out,
       and_34_out, and_35_out, and_36_out, and_37_out, and_38_out, and_39_out, and_40_out, and_41_out,
       and_42_out, and_43_out, and_44_out, and_45_out, and_46_out, and_47_out, and_48_out, not_1_out,
       not_2_out, not_3_out, not_4_out, not_5_out, not_6_out, not_7_out, not_8_out, not_9_out, not_10_out,
       not_11_out, not_12_out, not_13_out, not_14_out, not_15_out, not_16_out, not_17_out, not_18_out,
       not_19_out, not_20_out, not_21_out, not_22_out, not_23_out, not_24_out, not_25_out, not_26_out,
       not_27_out, not_28_out, not_29_out, not_30_out, not_31_out, not_32_out, or_1_out, or_2_out, or_4_out,
       or_5_out, or_7_out, or_8_out, or_10_out, or_11_out, or_13_out, or_14_out, or_16_out, or_17_out,
       or_19_out, or_20_out, or_22_out;

  not not_1 (not_1_out, A0);
  not not_2 (not_2_out, B0);
  and and_1 (and_1_out, not_1_out, B0);
  or or_1 (or_1_out, and_1_out, and_2_out);
  and and_2 (and_2_out, A0, not_2_out);
  and and_3 (and_3_out, A0, Cin);
  and and_4 (and_4_out, A0, B0);
  not not_3 (not_3_out, or_1_out);
  not not_4 (not_4_out, Cin);
  or or_2 (or_2_out, and_3_out, and_4_out);
  and and_5 (and_5_out, not_3_out, Cin);
  and and_6 (and_6_out, or_1_out, not_4_out);
  or or_3 (S0, and_5_out, and_6_out);
  not not_5 (not_5_out, A1);
  and and_7 (and_7_out, not_5_out, B1);
  and and_8 (and_8_out, A1, not_6_out);
  not not_6 (not_6_out, B1);
  and and_9 (and_9_out, A1, or_2_out);
  and and_10 (and_10_out, A1, B1);
  or or_4 (or_4_out, and_7_out, and_8_out);
  or or_5 (or_5_out, and_9_out, and_10_out);
  not not_7 (not_7_out, or_4_out);
  not not_8 (not_8_out, or_2_out);
  and and_11 (and_11_out, not_7_out, or_2_out);
  and and_12 (and_12_out, or_4_out, not_8_out);
  or or_6 (S1, and_11_out, and_12_out);
  not not_9 (not_9_out, A2);
  not not_10 (not_10_out, B2);
  and and_13 (and_13_out, not_9_out, B2);
  and and_14 (and_14_out, A2, not_10_out);
  and and_15 (and_15_out, A2, or_5_out);
  and and_16 (and_16_out, A2, B2);
  or or_7 (or_7_out, and_13_out, and_14_out);
  not not_11 (not_11_out, or_7_out);
  not not_12 (not_12_out, or_5_out);
  or or_8 (or_8_out, and_15_out, and_16_out);
  and and_17 (and_17_out, not_11_out, or_5_out);
  and and_18 (and_18_out, or_7_out, not_12_out);
  or or_9 (S2, and_17_out, and_18_out);
  not not_13 (not_13_out, A3);
  not not_14 (not_14_out, B3);
  and and_19 (and_19_out, not_13_out, B3);
  and and_20 (and_20_out, A3, not_14_out);
  and and_21 (and_21_out, A3, or_8_out);
  and and_22 (and_22_out, A3, B3);
  or or_10 (or_10_out, and_19_out, and_20_out);
  or or_11 (or_11_out, and_21_out, and_22_out);
  not not_15 (not_15_out, or_10_out);
  and and_23 (and_23_out, not_15_out, or_8_out);
  and and_24 (and_24_out, or_10_out, not_16_out);
  not not_16 (not_16_out, or_8_out);
  or or_12 (S3, and_23_out, and_24_out);
  not not_17 (not_17_out, A4);
  not not_18 (not_18_out, B4);
  and and_25 (and_25_out, not_17_out, B4);
  or or_13 (or_13_out, and_25_out, and_26_out);
  and and_26 (and_26_out, A4, not_18_out);
  and and_27 (and_27_out, A4, or_11_out);
  and and_28 (and_28_out, A4, B4);
  not not_19 (not_19_out, or_13_out);
  not not_20 (not_20_out, or_11_out);
  or or_14 (or_14_out, and_27_out, and_28_out);
  and and_29 (and_29_out, not_19_out, or_11_out);
  and and_30 (and_30_out, or_13_out, not_20_out);
  or or_15 (S4, and_29_out, and_30_out);
  not not_21 (not_21_out, A5);
  not not_22 (not_22_out, B5);
  and and_31 (and_31_out, not_21_out, B5);
  and and_32 (and_32_out, A5, not_22_out);
  and and_33 (and_33_out, A5, or_14_out);
  and and_34 (and_34_out, A5, B5);
  not not_23 (not_23_out, or_16_out);
  or or_16 (or_16_out, and_31_out, and_32_out);
  not not_24 (not_24_out, or_14_out);
  or or_17 (or_17_out, and_33_out, and_34_out);
  and and_35 (and_35_out, not_23_out, or_14_out);
  and and_36 (and_36_out, or_16_out, not_24_out);
  or or_18 (S5, and_35_out, and_36_out);
  not not_25 (not_25_out, A6);
  and and_37 (and_37_out, not_25_out, B6);
  and and_38 (and_38_out, A6, not_26_out);
  not not_26 (not_26_out, B6);
  and and_39 (and_39_out, A6, or_17_out);
  and and_40 (and_40_out, A6, B6);
  or or_19 (or_19_out, and_37_out, and_38_out);
  or or_20 (or_20_out, and_39_out, and_40_out);
  not not_27 (not_27_out, or_19_out);
  not not_28 (not_28_out, or_17_out);
  and and_41 (and_41_out, not_27_out, or_17_out);
  or or_21 (S6, and_41_out, and_42_out);
  and and_42 (and_42_out, or_19_out, not_28_out);
  not not_29 (not_29_out, A7);
  not not_30 (not_30_out, B7);
  and and_43 (and_43_out, not_29_out, B7);
  and and_44 (and_44_out, A7, not_30_out);
  and and_45 (and_45_out, A7, or_20_out);
  and and_46 (and_46_out, A7, B7);
  not not_31 (not_31_out, or_22_out);
  or or_22 (or_22_out, and_43_out, and_44_out);
  not not_32 (not_32_out, or_20_out);
  or or_23 (Cout, and_45_out, and_46_out);
  and and_47 (and_47_out, not_31_out, or_20_out);
  and and_48 (and_48_out, or_22_out, not_32_out);
  or or_24 (S7, and_47_out, and_48_out);

  // Notes on the sheet:
  //   total
  //   1º número
  //   2º número
endmodule
