// Logisim project somador-completo-8-bits.circ as structural Verilog: 1 circuit, main circuit main
module main (
  input  Cin,
  input  A0,
  input  A7,
  input  A6,
  input  A5,
  input  A4,
  input  A3,
  input  A2,
  input  A1,
  input  B7,
  input  B6,
  input  B5,
  input  B4,
  input  B3,
  input  B2,
  input  B1,
  input  B0,
  output Cout,
  output S7,
  output S6,
  output S5,
  output S4,
  output S3,
  output S2,
  output S1,
  output S0
);

  wire and_1_out, and_2_out, and_3_out, and_4_out, and_5_out, and_6_out, and_7_out, and_8_out, and_9_out,
       and_10_out, and_11_out, and_12_out, and_13_out, and_14_out, and_15_out, and_16_out, or_1_out,
       or_2_out, or_3_out, or_4_out, or_5_out, or_6_out, or_7_out, xor_1_out, xor_3_out, xor_5_out,
       xor_7_out, xor_9_out, xor_11_out, xor_13_out, xor_15_out;

  xor xor_1 (xor_1_out, A0, B0);
  xor xor_2 (S0, xor_1_out, Cin);
  and and_1 (and_1_out, xor_1_out, Cin);
  and and_2 (and_2_out, A0, B0);
  or or_1 (or_1_out, and_1_out, and_2_out);
  xor xor_3 (xor_3_out, A1, B1);
  xor xor_4 (S1, xor_3_out, or_1_out);
  and and_3 (and_3_out, xor_3_out, or_1_out);
  and and_4 (and_4_out, A1, B1);
  or or_2 (or_2_out, and_3_out, and_4_out);
  xor xor_5 (xor_5_out, A2, B2);
  xor xor_6 (S2, xor_5_out, or_2_out);
  and and_5 (and_5_out, xor_5_out, or_2_out);
  and and_6 (and_6_out, A2, B2);
  or or_3 (or_3_out, and_5_out, and_6_out);
  xor xor_7 (xor_7_out, A3, B3);
  xor xor_8 (S3, xor_7_out, or_3_out);
  and and_7 (and_7_out, xor_7_out, or_3_out);
  and and_8 (and_8_out, A3, B3);
  or or_4 (or_4_out, and_7_out, and_8_out);
  xor xor_9 (xor_9_out, A4, B4);
  xor xor_10 (S4, xor_9_out, or_4_out);
  and and_9 (and_9_out, xor_9_out, or_4_out);
  and and_10 (and_10_out, A4, B4);
  or or_5 (or_5_out, and_9_out, and_10_out);
  xor xor_11 (xor_11_out, A5, B5);
  xor xor_12 (S5, xor_11_out, or_5_out);
  and and_11 (and_11_out, xor_11_out, or_5_out);
  and and_12 (and_12_out, A5, B5);
  or or_6 (or_6_out, and_11_out, and_12_out);
  xor xor_13 (xor_13_out, A6, B6);
  and and_13 (and_13_out, xor_13_out, or_6_out);
  and and_14 (and_14_out, A6, B6);
  xor xor_14 (S6, xor_13_out, or_6_out);
  or or_7 (or_7_out, and_13_out, and_14_out);
  xor xor_15 (xor_15_out, A7, B7);
  xor xor_16 (S7, xor_15_out, or_7_out);
  and and_15 (and_15_out, xor_15_out, or_7_out);
  and and_16 (and_16_out, A7, B7);
  or or_8 (Cout, and_15_out, and_16_out);

  // Notes on the sheet:
  //   total
  //   1º número
  //   2º número
  //   0
  //   1
  //   2
  //   3
  //   4
  //   5
  //   6
  //   7
endmodule
