// Logisim project somador-subtrator-8-bit.circ as structural Verilog: 4 circuits, main circuit somador-subtrator-8-bits
module somador_subtrator_8_bits (
  input  M,
  input  A7,
  input  A6,
  input  A5,
  input  A4,
  input  A3,
  input  A2,
  input  A1,
  input  A0,
  input  B7,
  input  B6,
  input  B5,
  input  B4,
  input  B3,
  input  B2,
  input  B1,
  input  B0,
  output Cout,
  output S7,
  output S6,
  output S5,
  output S4,
  output S3,
  output S2,
  output S1,
  output S0
);

  wire full_adder_1_cout, full_adder_2_cout, full_adder_3_cout, full_adder_4_cout, full_adder_5_cout,
       full_adder_6_cout, full_adder_7_cout, xor_1_out_3, xor_2_out_3, xor_3_out_3, xor_4_out_3, xor_5_out_3,
       xor_6_out_3, xor_7_out_3, xor_8_out_3;

  XOR xor_1 (.in_1(B0), .in_2(M), .out_3(xor_1_out_3));
  XOR xor_2 (.in_1(B1), .in_2(M), .out_3(xor_2_out_3));
  XOR xor_3 (.in_1(B2), .in_2(M), .out_3(xor_3_out_3));
  XOR xor_4 (.in_1(B3), .in_2(M), .out_3(xor_4_out_3));
  XOR xor_5 (.in_1(B4), .in_2(M), .out_3(xor_5_out_3));
  XOR xor_6 (.in_1(B5), .in_2(M), .out_3(xor_6_out_3));
  XOR xor_7 (.in_1(B6), .in_2(M), .out_3(xor_7_out_3));
  XOR xor_8 (.in_1(B7), .in_2(M), .out_3(xor_8_out_3));
  Full_Adder full_adder_1 (.A(M), .B(A0), .Cin(xor_1_out_3), .S(S0), .Cout(full_adder_1_cout));
  Full_Adder full_adder_2 (.A(full_adder_1_cout), .B(A1), .Cin(xor_2_out_3), .S(S1), .Cout(full_adder_2_cout));
  Full_Adder full_adder_3 (.A(full_adder_2_cout), .B(A2), .Cin(xor_3_out_3), .S(S2), .Cout(full_adder_3_cout));
  Full_Adder full_adder_4 (.A(full_adder_3_cout), .B(A3), .Cin(xor_4_out_3), .S(S3), .Cout(full_adder_4_cout));
  Full_Adder full_adder_5 (.A(full_adder_4_cout), .B(A4), .Cin(xor_5_out_3), .S(S4), .Cout(full_adder_5_cout));
  Full_Adder full_adder_6 (.A(full_adder_5_cout), .B(A5), .Cin(xor_6_out_3), .S(S5), .Cout(full_adder_6_cout));
  Full_Adder full_adder_7 (.A(full_adder_6_cout), .B(A6), .Cin(xor_7_out_3), .S(S6), .Cout(full_adder_7_cout));
  Full_Adder full_adder_8 (.A(full_adder_7_cout), .B(A7), .Cin(xor_8_out_3), .S(S7), .Cout(Cout));
endmodule

module XOR (
  input  in_1,
  input  in_2,
  output out_3
);

  wire and_1_out, and_2_out, not_1_out, not_2_out;

  not not_1 (not_1_out, in_1);
  not not_2 (not_2_out, in_2);
  and and_1 (and_1_out, not_1_out, in_2);
  and and_2 (and_2_out, in_1, not_2_out);
  or or_1 (out_3, and_1_out, and_2_out);
endmodule

module Half_adder (
  input  A,
  input  B,
  output Sum,
  output Cout
);

  XOR xor_1 (.in_1(A), .in_2(B), .out_3(Sum));
  and and_1 (Cout, B, A);
endmodule

module Full_Adder (
  input  A,
  input  B,
  input  Cin,
  output S,
  output Cout
);

  wire half_adder_1_cout, half_adder_1_sum, half_adder_2_cout;

  Half_adder half_adder_1 (.A(A), .B(B), .Sum(half_adder_1_sum), .Cout(half_adder_1_cout));
  Half_adder half_adder_2 (.A(half_adder_1_sum), .B(Cin), .Sum(S), .Cout(half_adder_2_cout));
  or or_1 (Cout, half_adder_2_cout, half_adder_1_cout);
endmodule
